# Fritzing sketch 40106_Osc1 (saved by Fritzing 0.9.4)
breadboards: 1

parts:
  CD40106 = Hex Inverter Schmitt Trigger SN74HC14 [package="DIP (Dual Inline)"]
  part = DC Power [voltage=9V]
  R1 = Rotary Potentiometer (Small) [maximum_resistance=10kΩ package=THT]
  C1 = Ceramic Capacitor [capacitance=100nF package="100 mil [THT, multilayer]"]
  audio_jack = Audio Jack (TRS) 3.5mm [package="PG203J [THT]"]

nets:
  N1: CD40106.1A, R1.wiper, C1.1
  N2: CD40106.1Y, R1.leg2, audio_jack.Ring, audio_jack.Tip
  GND: CD40106.GND, part.V-, C1.0, audio_jack.Sleeve
  N3: CD40106.VCC, part.V+
