# Fritzing sketch 40106_Osc2 (saved by Fritzing 0.9.4)
breadboards: 1

parts:
  V1 = DC Power [voltage=9V]
  C1 = Ceramic Capacitor [capacitance=100nF package="100 mil [THT, multilayer]"]
  audio_jack = Audio Jack (TRS) 3.5mm [package="PG203J [THT]"]
  R1 = Photocell (LDR) [package=THT]
  CD40106 = Hex Inverter Schmitt Trigger SN74HC14 [package="DIP (Dual Inline)"]

nets:
  N1: V1.V+, CD40106.VCC
  GND: V1.V-, C1.0, audio_jack.Sleeve, CD40106.GND
  N2: C1.1, R1.pin_0, CD40106.1A
  N3: audio_jack.Ring, audio_jack.Tip, R1.pin_1, CD40106.1Y
