# Fritzing sketch 4051_photocells (saved by Fritzing 0.9.4)
breadboards: 1

parts:
  IC1 = 74HC4051 [package=so16]
  R16 = Resistor [tolerance=±5% resistance=10k package=THT]
  U1 = Arduino Uno (Rev3)
  R15 = Photocell (LDR) [package=THT]
  R13 = Photocell (LDR) [package=THT]
  R11 = Photocell (LDR) [package=THT]
  R9 = Photocell (LDR) [package=THT]
  R1 = Photocell (LDR) [package=THT]
  R3 = Photocell (LDR) [package=THT]
  R5 = Photocell (LDR) [package=THT]
  R7 = Photocell (LDR) [package=THT]
  R14 = Resistor [tolerance=±5% resistance=10k package=THT]
  R12 = Resistor [tolerance=±5% resistance=10k package=THT]
  R10 = Resistor [tolerance=±5% resistance=10k package=THT]
  R8 = Resistor [tolerance=±5% resistance=10k package=THT]
  R6 = Resistor [tolerance=±5% resistance=10k package=THT]
  R4 = Resistor [tolerance=±5% resistance=10k package=THT]
  R2 = Resistor [tolerance=±5% resistance=10k package=THT]

nets:
  N1: IC1.IO4, R9.pin_1, R10.Pin_1
  N2: IC1.IO6, R13.pin_1, R14.Pin_1
  N3: IC1.IO, U1.A0
  N4: IC1.IO7, R16.Pin_1, R15.pin_1
  N5: IC1.IO5, R11.pin_1, R12.Pin_1
  VSS: IC1.INH, IC1.VEE, IC1.VSS, R16.Pin_0, U1.GND, R14.Pin_0, R12.Pin_0, R10.Pin_0, R8.Pin_1, R6.Pin_1, R4.Pin_1, R2.Pin_1
  N6: IC1.C, U1.D9_PWM
  N7: IC1.B, U1.D10_PWM/SS
  N8: IC1.A, U1.D11_PWM/MOSI
  N9: IC1.IO3, R7.pin_1, R8.Pin_0
  N10: IC1.IO0, R1.pin_1, R2.Pin_0
  N11: IC1.IO1, R3.pin_1, R4.Pin_0
  N12: IC1.IO2, R5.pin_1, R6.Pin_0
  VDD: IC1.VDD, U1.5V, R15.pin_0, R13.pin_0, R11.pin_0, R9.pin_0, R1.pin_0, R3.pin_0, R5.pin_0, R7.pin_0
