# Fritzing sketch Shift_Register_LEDs (saved by Fritzing 0.9.4)
circuit board: 6.88566cm x 5.36311cm
breadboards: 2

parts:
  R7 = Resistor [resistance=560 tolerance=±5% package=THT]
  R6 = Resistor [resistance=560 tolerance=±5% package=THT]
  R5 = Resistor [resistance=560 tolerance=±5% package=THT]
  R8 = Resistor [resistance=560 tolerance=±5% package=THT]
  R4 = Resistor [resistance=560 tolerance=±5% package=THT]
  R3 = Resistor [resistance=560 tolerance=±5% package=THT]
  R2 = Resistor [resistance=560 tolerance=±5% package=THT]
  R1 = Resistor [resistance=560 tolerance=±5% package=THT]
  LED10 = LED - 5mm [color="Red (633nm)" package="5 mm [THT]"]
  LED11 = LED - 5mm [color="Red (633nm)" package="5 mm [THT]"]
  LED12 = LED - 5mm [color="Red (633nm)" package="5 mm [THT]"]
  LED13 = LED - 5mm [color="Red (633nm)" package="5 mm [THT]"]
  LED14 = LED - 5mm [color="Red (633nm)" package="5 mm [THT]"]
  LED15 = LED - 5mm [color="Red (633nm)" package="5 mm [THT]"]
  LED16 = LED - 5mm [color="Red (633nm)" package="5 mm [THT]"]
  LED17 = LED - 5mm [color="Red (633nm)" package="5 mm [THT]"]
  74HC595 = 74HC595 [package="DIP16 [THT]"]
  C1 = Ceramic Capacitor [capacitance=100nF rated_voltage=35V package="200 mil [THT, multilayer]"]
  Arduino1 = Arduino Uno (Rev3)

nets:
  N1: R7.Pin_0, LED14.anode
  N2: R7.Pin_1, 74HC595.Q6
  N3: R6.Pin_0, LED10.anode
  N4: R6.Pin_1, 74HC595.Q5
  N5: R5.Pin_0, LED12.anode
  N6: R5.Pin_1, 74HC595.Q4
  N7: R8.Pin_0, LED11.anode
  N8: R8.Pin_1, 74HC595.Q7
  N9: R4.Pin_0, LED13.anode
  N10: R4.Pin_1, 74HC595.Q3
  N11: R3.Pin_0, LED15.anode
  N12: R3.Pin_1, 74HC595.Q2
  N13: R2.Pin_0, LED16.anode
  N14: R2.Pin_1, 74HC595.Q1
  N15: R1.Pin_0, LED17.anode
  N16: R1.Pin_1, 74HC595.Q0
  GND: LED10.cathode, LED11.cathode, LED12.cathode, LED13.cathode, LED14.cathode, LED15.cathode, LED16.cathode, LED17.cathode, 74HC595.GND, 74HC595.OE, C1.1, Arduino1.GND
  VCC: 74HC595.MR, 74HC595.VCC, Arduino1.5V
  N17: 74HC595.SH_CP, Arduino1.D12/MISO
  N18: 74HC595.ST_CP, C1.0, Arduino1.D8
  N19: 74HC595.DS, Arduino1.D11_PWM/MOSI

notes:
  In this project, a 74HC595 shift register is used to control 8 LEDs with just 3 Arduino pins.
  Related example: http://www.arduino.cc/en/Tutorial/ShiftOut

// code stored in the sketch: Shift_Register.ino
/*
  Shift Register Example
 for 74HC595 shift register

 This sketch turns reads serial input and uses it to set the pins
 of a 74HC595 shift register.

 Hardware:
 * 74HC595 shift register attached to pins 2, 3, and 4 of the Arduino,
 as detailed below.
 * LEDs attached to each of the outputs of the shift register

 Created 22 May 2009
 Created 23 Mar 2010
 by Tom Igoe

 */

//Pin connected to latch pin (ST_CP) of 74HC595
const int latchPin = 8;
//Pin connected to clock pin (SH_CP) of 74HC595
const int clockPin = 12;
////Pin connected to Data in (DS) of 74HC595
const int dataPin = 11;

void setup() {
  //set pins to output because they are addressed in the main loop
  pinMode(latchPin, OUTPUT);
  pinMode(dataPin, OUTPUT);  
  pinMode(clockPin, OUTPUT);
  Serial.begin(9600);
  Serial.println("reset");
}

void loop() {
  if (Serial.available() > 0) {
    // ASCII '0' through '9' characters are
    // represented by the values 48 through 57.
    // so if the user types a number from 0 through 9 in ASCII, 
    // you can subtract 48 to get the actual value:
    int bitToSet = Serial.read() - 48;

  // write to the shift register with the correct bit set high:
    registerWrite(bitToSet, HIGH);
  }
}

// This method sends bits to the shift register:

void registerWrite(int whichPin, int whichState) {
// the bits you want to send
  byte bitsToSend = 0;

  // turn off the output so the pins don't light up
  // while you're shifting bits:
  digitalWrite(latchPin, LOW);

  // turn on the next highest bit in bitsToSend:
  bitWrite(bitsToSend, whichPin, whichState);

  // shift the bits out:
  shiftOut(dataPin, clockPin, MSBFIRST, bitsToSend);

    // turn on the output so the LEDs can light up:
  digitalWrite(latchPin, HIGH);

}
