# Fritzing sketch IRSensor (saved by Fritzing 0.8.5b)
breadboards: 1

parts:
  Part1 = Arduino Uno (Rev3)
  J1 = Infrared Proximity Sensor

nets:
  N1: Part1.A0, J1.Vout
  GND: Part1.GND, J1.GND
  5V: Part1.5V, J1.Vcc
