# Fritzing sketch photocell (saved by Fritzing 0.9.4)
breadboards: 1

parts:
  U1 = Arduino Uno (Rev3)
  R1 = Resistor [tolerance=±5% resistance=10k package=THT]
  R2 = Photocell (LDR) [package=THT]

nets:
  N1: U1.A0, R1.Pin_1, R2.pin_0
  N2: U1.5V, R2.pin_1
  N3: U1.GND, R1.Pin_0
