# Fritzing sketch Potentiometer_LED (saved by Fritzing 0.9.4)
circuit board: 6.88566cm x 5.36311cm
breadboards: 1

parts:
  LED2 = LED - 5mm [color="Red (633nm)" package="5 mm [THT]"]
  R1 = Rotary Potentiometer (Small) [maximum_resistance=100kΩ package=THT]
  Arduino2 = Arduino Uno (Rev3)
  R2 = Resistor [tolerance=±5% resistance=1k package=THT]

nets:
  N1: LED2.cathode, R1.leg1, Arduino2.GND
  N2: LED2.anode, R2.Pin_1
  N3: R1.wiper, Arduino2.A0
  N4: R1.leg2, Arduino2.5V
  N5: Arduino2.D9_PWM, R2.Pin_0
