# Fritzing sketch Button (saved by Fritzing 0.8.5b)
circuit board: 6.88566cm x 5.36311cm
breadboards: 1

parts:
  LED1 = LED - 5mm [color="Red (633nm)" package="5 mm [THT]"]
  R1 = Resistor [tolerance=±5% resistance=10k package=THT]
  S1 = Pushbutton [package="[THT]"]
  Arduino1 = Arduino Uno (Rev3)

nets:
  N1: LED1.cathode, R1.Pin_1, Arduino1.GND
  N2: LED1.anode, Arduino1.D13/SCK
  N3: R1.Pin_0, S1.Pin_3, S1.Pin_4, Arduino1.D2
  N4: S1.Pin_1, S1.Pin_2, Arduino1.5V

notes:
  In this example, a pushbutton is used as a digital input and an LED is a digital output.
  Related example: http://arduino.cc/en/Tutorial/Button
