# Fritzing sketch DigitalInOut (saved by Fritzing 0.8.5b)
breadboards: 1

parts:
  Arduino = Arduino Uno (Rev3)
  S1 = Pushbutton [package="[THT]"]
  R1 = Resistor [tolerance=±5% resistance=10k package=THT]
  R2 = Resistor [tolerance=±5% resistance=220 package=THT]
  R3 = Resistor [tolerance=±5% resistance=220 package=THT]
  LED1 = LED - 5mm [color="Red (633nm)" package="5 mm [THT]"]
  LED2 = LED - 5mm [color="Yellow (585nm)" package="5 mm [THT]"]

nets:
  N1: Arduino.D2, S1.Pin_3, S1.Pin_4, R1.Pin_1
  N2: Arduino.D3_PWM, R3.Pin_0
  N3: Arduino.D4, R2.Pin_0
  N4: Arduino.5V, S1.Pin_1, S1.Pin_2
  N5: Arduino.GND, R1.Pin_0, LED1.cathode, LED2.cathode
  N6: R2.Pin_1, LED1.anode
  N7: R3.Pin_1, LED2.anode

notes:
  Digital Input and Output
  - Study the digital input and output demo program and hookup
  - Modify it so you use different inputs and outputs than the demo
  - hook up the Arduino board in the modified form
  - write the program in modified form
  - upload to Arduino
  - run it
  Looked at the tutorial on the ITP physcomp labs site: http://itp.nyu.edu/physcomp/Labs/DigitalInOut
