# Fritzing sketch slide_switch (saved by Fritzing 0.9.4)
breadboards: 1

parts:
  S1 = Toggle Switch [package=THT]
  U1 = Arduino Nano (Rev3.0)
  R1 = Resistor [tolerance=±5% resistance=10k package=THT]
  C1 = Ceramic Capacitor [capacitance=100nF package="100 mil [THT, multilayer]"]
  R2 = Resistor [tolerance=±5% resistance=220 package=THT]
  LED1 = LED - 5mm [color="Red (633nm)" package="5 mm [THT]"]

nets:
  N1: S1.L1, U1.GND, R1.Pin_0, C1.1, LED1.cathode
  N2: S1.COM, U1.D2, R1.Pin_1, C1.0
  N3: S1.L2, U1.3V3
  N4: U1.D3, R2.Pin_0
  N5: R2.Pin_1, LED1.anode
