# Fritzing sketch SimpleDCMotorControl (saved by Fritzing 0.8.5b)
breadboards: 1

parts:
  Arduino = Arduino Uno (Rev3)
  M1 = DC Motor
  Q1 = NPN-Transistor [package="TO92 [THT]"]
  R1 = Resistor [tolerance=±5% resistance=1k package=THT]
  D1_(snubber_diode) = Rectifier Diode [part_number=1N4001 package="300 mil [THT]"]
  JACK1 = 2.1mm Barrel Jack with Terminal Block

nets (from the breadboard view):
  N1: Arduino.D3_PWM, R1.Pin_1
  N2: Arduino.GND, D1_(snubber_diode).anode, JACK1.NEG
  N3: M1.pin_1, JACK1.POS
  N4: M1.pin_2, Q1.C
  N5: Q1.E, D1_(snubber_diode).cathode
  N6: Q1.B, R1.Pin_0

notes:
  Simple DC Motor control circuuit
  How would you vary the speed of the motor from the Arduino?
  Try adding a photocell or FSR and use to control the speed of the motor
