# Fritzing sketch DC_Motor_Nano (saved by Fritzing 0.9.4)
breadboards: 1

parts:
  R1 = Resistor [tolerance=±5% resistance=1k package=THT]
  D1 = Rectifier Diode [part_number=1N4001 package="300 mil [THT]"]
  R2 = Trimmer Potentiometer [maximum_resistance=10kΩ package=THT]
  Q1 = NPN-Transistor [part_number=2n3904 package="TO92 [THT]"]
  U1 = Arduino Nano (Rev3.0)
  M1 = Vibration Motor- ROB-08449 [package=vibe-motor-10mm]

nets:
  N1: R1.Pin_0, U1.D9
  N2: R1.Pin_1, Q1.B
  N3: D1.cathode, Q1.C, M1.-
  N4: D1.anode, R2.leg1, Q1.E, U1.GND
  N5: R2.wiper, U1.A0
  N6: R2.leg2, U1.3V3, M1.+
