# Fritzing sketch DC_motor_Variable_Resistor_NoArduino (saved by Fritzing 0.9.4)
breadboards: 1

parts:
  R1 = Resistor [resistance=1k tolerance=±5% package=THT]
  Q1 = NPN-Transistor [package="TO92 [THT]"]
  JACK1 = 2.1mm Barrel Jack with Terminal Block
  D1 = Rectifier Diode [part_number=1N4001 package="300 mil [THT]"]
  M1 = DC Motor
  R3 = Photocell (LDR) [package=THT]
  R4 = Resistor [tolerance=±5% resistance=10k package=THT]
  U1 = Voltage Regulator - 5V [package="TO220 [THT]"]

nets:
  N1: R1.Pin_0, Q1.B
  N2: R1.Pin_1, R3.pin_0, R4.Pin_1
  N3: Q1.E, JACK1.NEG, D1.anode, R4.Pin_0, U1.GND
  N4: Q1.C, D1.cathode, M1.pin_2
  N5: JACK1.POS, M1.pin_1, U1.input_voltage
  N6: R3.pin_1, U1.output_voltage
