# Fritzing sketch AnalogInputToServo (saved by Fritzing 0.9.4)
circuit board: 6.88566cm x 5.36311cm
breadboards: 1

parts:
  J1 = Basic Servo
  Arduino2 = Arduino Uno (Rev3)
  R1 = Photocell (LDR) [package=THT]
  R2 = Resistor [tolerance=±5% resistance=10k package=THT]

nets:
  GND: J1.gnd, Arduino2.GND, R2.Pin_0
  VCC: J1.vcc, Arduino2.5V, R1.pin_1
  N1: J1.pulse, Arduino2.D9_PWM
  N2: Arduino2.A2, R1.pin_0, R2.Pin_1
