# Fritzing sketch Flora_LSM303 (saved by Fritzing 0.9.4)
breadboards: 1

parts:
  A1 = Flora LSM303 Compass+Accel
  U1 = Arduino Uno (Rev3)

nets:
  GND: A1.GND, U1.GND
  N1: A1.SCL, U1.A5/SCL
  N2: A1.SDA, U1.A4/SDA
  3.3V: A1.3.3V, U1.3V3

notes:
  A4 = SDA (data)
  A5 = SCL (clock)

custom parts:
  Flora LSM303 Compass+Accel: Add motion and direction sensing to your wearable FLORA project with this high precision 3-axis Accelerometer+Compass sensor. Inside are two sensors, one is a classic 3-axis accelerometer, which can tell you which direction is down towards the Earth (by measuring gravity) or how fast the board is accelerating in 3D space. The other is a magnetometer that can sense where the strongest magnetic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
