# Fritzing sketch CapSense (saved by Fritzing 0.9.4)
breadboards: 1

parts:
  U1 = Arduino Uno (Rev3)
  R1 = Resistor [tolerance=±5% resistance=1M package=THT]
  C1 = Ceramic Capacitor [capacitance=0.1nF package="100 mil [THT, multilayer]"]
  J1 = female pin header, 1 pin [form="♀ (female)"]
  R2 = Resistor [tolerance=±5% resistance=1k package=THT]

nets:
  N1: U1.GND, C1.1
  N2: U1.D2, R1.Pin_1
  N3: U1.D3_PWM, C1.0, R2.Pin_0
  N4: R1.Pin_0, J1.pin1, R2.Pin_1

notes:
  copper foil or other conductive material
