# Fritzing sketch Capacitance (saved by Fritzing 0.8.5b)
breadboards: 1

parts:
  R1 = Resistor [tolerance=±5% resistance=1M package=THT]
  R7 = Resistor [tolerance=±5% resistance=10k package=THT]
  Out1 = female pin header, 1 pin [form="♀ (female)"]
  R2 = Resistor [tolerance=±5% resistance=1M package=THT]
  R3 = Resistor [tolerance=±5% resistance=1M package=THT]
  R4 = Resistor [tolerance=±5% resistance=1M package=THT]
  R5 = Resistor [tolerance=±5% resistance=1M package=THT]
  R6 = Resistor [tolerance=±5% resistance=1M package=THT]
  Out2 = female pin header, 1 pin [form="♀ (female)"]
  Electrodes/Plants = screw terminal, 6 pins
  R8 = Resistor [tolerance=±5% resistance=10k package=THT]
  Out3 = female pin header, 1 pin [form="♀ (female)"]
  R9 = Resistor [tolerance=±5% resistance=10k package=THT]
  Out4 = female pin header, 1 pin [form="♀ (female)"]
  R10 = Resistor [tolerance=±5% resistance=10k package=THT]
  Out5 = female pin header, 1 pin [form="♀ (female)"]
  R11 = Resistor [tolerance=±5% resistance=10k package=THT]
  Out6 = female pin header, 1 pin [form="♀ (female)"]
  R12 = Resistor [tolerance=±5% resistance=10k package=THT]
  Power = Screw terminal - 2 pins [package=THT]  # not connected

nets:
  5V: R1.Pin_0, R2.Pin_0, R3.Pin_0, R4.Pin_0, R5.Pin_0, R6.Pin_0
  N1: R1.Pin_1, R7.Pin_0, Electrodes/Plants.pin1
  N2: R7.Pin_1, Out1.pin1
  N3: R2.Pin_1, Electrodes/Plants.pin2, R8.Pin_0
  N4: R3.Pin_1, Electrodes/Plants.pin3, R9.Pin_0
  N5: R4.Pin_1, Electrodes/Plants.pin4, R10.Pin_0
  N6: R5.Pin_1, Electrodes/Plants.pin5, R11.Pin_0
  N7: R6.Pin_1, Electrodes/Plants.pin6, R12.Pin_0
  N8: Out2.pin1, R8.Pin_1
  N9: Out3.pin1, R9.Pin_1
  N10: Out4.pin1, R10.Pin_1
  N11: Out5.pin1, R11.Pin_1
  N12: Out6.pin1, R12.Pin_1
