# Fritzing sketch GSR (saved by Fritzing 0.8.3b)
circuit board: 6.8cm x 6cm
breadboards: 1

parts:
  R2 = Resistor [tolerance=±5% resistance=3M package=THT]
  R3 = Resistor [tolerance=±5% resistance=750k package=THT]
  U1_(LM358) = LM358 [package=dip08]
  R6 = Resistor [tolerance=±5% resistance=1k package=THT]
  R7 = Resistor [tolerance=±5% resistance=1k package=THT]
  R4 = Trimmer Potentiometer [maximum_resistance=240kΩ package=THT]
  R1 = Trimmer Potentiometer [maximum_resistance=500kΩ package=THT]
  R5 = Resistor [tolerance=±5% resistance=680k package=THT]
  R8 = Resistor [tolerance=±5% resistance=3.3k package=THT]
  C1 = Electrolytic Capacitor [capacitance=1µF package="100 mil [THT, electrolytic]"]
  Out = female pin header, 1 pin [form="♀ (female)"]
  Electrodes = screw terminal, 2 pins
  Power = screw terminal, 2 pins
  GND = female pin header, 1 pin [form="♀ (female)"]
  R9 = Resistor [tolerance=±5% resistance=4.7k package=THT]

nets:
  N1: R2.Pin_0, R3.Pin_1, R1.wiper
  N2: R2.Pin_1, R7.Pin_1, Electrodes.pin2
  N3: R3.Pin_0, R4.leg2
  N4: U1_(LM358).G$1_OUT, R8.Pin_0, R9.Pin_1
  N5: U1_(LM358).G$1_-IN, R6.Pin_0, R8.Pin_1
  N6: U1_(LM358).G$1_+IN, R7.Pin_0
  GND: U1_(LM358).G$1_V-, R1.leg2, R5.Pin_1, C1.-, Electrodes.pin1, Power.pin2, GND.pin1
  5V: U1_(LM358).G$1_V+, R1.leg1, Power.pin1
  N7: R6.Pin_1, R4.wiper
  N8: R4.leg1, R5.Pin_0
  N9: C1.+, Out.pin1, R9.Pin_0

notes:
  Organic Oscillations, Galvanic Sensor
  Organic Oscillations
  galvanic sensor
  ecology.dprime.org
