# Fritzing sketch Infrared_distance (saved by Fritzing 0.9.4)
breadboards: 1

parts:
  U1 = Arduino Uno (Rev3)
  J1 = Infrared Proximity Sensor
  C1 = Electrolytic Capacitor [capacitance=10µF package="100 mil [THT, electrolytic]"]

nets:
  N1: U1.A0, J1.Vout
  GND: U1.GND, J1.GND, C1.-
  5V: U1.5V, J1.Vcc, C1.+
