# Fritzing sketch potentiometer (saved by Fritzing 0.9.4)
breadboards: 1

parts:
  R1 = Rotary Potentiometer (Small) [maximum_resistance=10kΩ package=THT]
  Arduino = Arduino Uno (Rev3)

nets:
  N1: R1.leg1, Arduino.5V
  N2: R1.wiper, Arduino.A0
  N3: R1.leg2, Arduino.GND
