# Fritzing sketch piezo (saved by Fritzing 0.8.5b)
breadboards: 1

parts:
  Piezo = Buzzer 12mm [package=buzzer-ccv-kit]
  R1 = Resistor [tolerance=±5% resistance=100k package=THT]
  D1 = Zener Diode [part_number="1N4732A - 5.1v" breakdown_voltage=12.1V package="Melf DO-213 AB [SMD]"]
  R2 = Resistor [tolerance=±5% resistance=1k package=THT]

nets:
  GND: Piezo.1, R1.Pin_1, D1.anode
  N1: Piezo.2, R1.Pin_0, D1.cathode, R2.Pin_0

notes:
  Piezo sensor
  R1 effects the sensitivity of the sensor (more resistance less sensitivity but also reduces cpacitance build up) Experiment with different values (10k - 1M)
  The 5.1v Zener diode (D1) ensures that we do not send more than 5v to the Arduino
  R2 limits the current going to the Arduino
  To Arduino Analog in
