# Fritzing sketch piezo_alt (saved by Fritzing 0.8.5b)
breadboards: 1

parts:
  Piezo = Buzzer 12mm [package=buzzer-ccv-kit]
  R1 = Resistor [tolerance=±5% resistance=100k package=THT]
  D1 = Zener Diode [part_number="1N4732A - 5.1v" breakdown_voltage=12.1V package="Melf DO-213 AB [SMD]"]
  U1 = LM 358 Dual Op-Amp [package="DIP8 [THT]"]
  R2 = Resistor [tolerance=±5% resistance=1k package=THT]
  R3 = Resistor [tolerance=±5% resistance=1M package=THT]
  analog_signal = BANANA_CONN [package=banana_conn]

nets:
  GND: Piezo.1, R1.Pin_1, D1.anode, U1.connector3, R2.Pin_0
  N1: Piezo.2, R1.Pin_0, D1.cathode, U1.connector2
  N2: U1.connector0, R3.Pin_1, analog_signal.1
  N3: U1.connector1, R2.Pin_1, R3.Pin_0
  5V: U1.connector7

notes:
  Piezo sensor (alt)
  This schematic includes an op-amp (operational amplifier) to boost the signal coming from the sensor (whic can sometimes be very low, e.g. in the millivolt range)
  R1 effects the sensitivity of the sensor (more resistance=less sensitivity but also reduces capacitance build up) Experiment with different values (10k - 1M)
  The 5.1v Zener diode (D1) ensures that we do not send more than 5v to the Arduino
  R2 & R3 affect the amplication factor of the op-amp. In this case the 1K and 1M resitors gives us an amplication factor of 1000
  To Arduino Analog in
