# Fritzing sketch Photocell_RC (saved by Fritzing 0.9.3b)
circuit board: 6.88566cm x 5.36311cm
breadboards: 2

parts:
  R1 = Photocell (LDR) [package=THT]
  R2 = Resistor [tolerance=±5% resistance=10k package=THT]
  Arduino1 = Arduino Uno (Rev3)
  R3 = Resistor [tolerance=±5% resistance=1k package=THT]
  C1 = Electrolytic Capacitor [capacitance=470µF voltage=25V package="100 mil [THT, electrolytic]"]

nets:
  N1: R1.pin_0, Arduino1.5V
  N2: R1.pin_1, R2.Pin_0, R3.Pin_0
  N3: R2.Pin_1, Arduino1.GND, C1.-
  N4: Arduino1.A0, R3.Pin_1, C1.+

notes:
  Photocell voltage divider with an RC filter added
  This example uses a rather large (470uF) capacitor for demonstration purposes. Try different values for R3 & C1 & see how the circuit behaves
  R1 (photocell)
  R3 & cap form RC filter
  R2 other side of voltage divider
