# Fritzing sketch PressureControlledFader (saved by Fritzing 0.9.4)
breadboards: 1

parts:
  R1 = Resistor [tolerance=±5% resistance=1k package=THT]
  R2 = Resistor [tolerance=±5% resistance=390k package=THT]
  MC = Arduino Uno (Rev3)
  J1 = female pin header, 1 pin [form="♀ (female)"]
  J2 = female pin header, 1 pin [form="♀ (female)"]
  Q1 = NPN-Transistor [part_number=P2N2222 package="TO92 [THT]"]
  R3 = Resistor [tolerance=±5% resistance=10k package=THT]

nets:
  N1: R1.Pin_0, J1.pin1
  N2: R1.Pin_1, MC.5V, R3.Pin_0
  GND: R2.Pin_0, MC.GND, Q1.E
  N3: R2.Pin_1, J2.pin1, Q1.B
  N4: MC.A0, Q1.C, R3.Pin_1

notes:
  place fingers here
