# Fritzing sketch Pressure_controlled_fader_nano (saved by Fritzing 0.9.4)
breadboards: 1

parts:
  U1 = Arduino Nano (Rev3.0)
  Q1 = TRANSISTOR_NPN [part_number=2n3904 package=to-92]
  LED1 = LED - 5mm [color="Red (633nm)" package="5 mm [THT]"]
  R1 = Resistor [tolerance=±5% resistance=220 package=THT]
  R2 = Resistor [tolerance=±5% resistance=1k package=THT]
  J1 = female pin header, 1 pin [form="♀ (female)"]
  J2 = female pin header, 1 pin [form="♀ (female)"]
  R3 = Resistor [tolerance=±5% resistance=100k package=THT]

nets:
  GND: U1.GND, Q1.E, R3.Pin_0
  N1: U1.A0, Q1.C, LED1.cathode
  N2: U1.3V3, R1.Pin_1, R2.Pin_1
  N3: Q1.B, J2.pin1, R3.Pin_1
  N4: LED1.anode, R1.Pin_0
  N5: R2.Pin_0, J1.pin1

notes:
  place fingers here
