# Fritzing sketch resistiveTouch (saved by Fritzing 0.9.3b)
breadboards: 1

parts:
  R1 = Rotary Potentiometer (Small) [maximum_resistance=10kΩ package=THT]
  C1 = Electrolytic Capacitor [capacitance=1µF package="100 mil [THT, electrolytic]"]
  J1 = female pin header, 1 pin [form="♀ (female)"]
  Part1 = Arduino Uno (Rev3)
  J2 = female pin header, 1 pin [form="♀ (female)"]

nets:
  GND: R1.leg1, C1.-, Part1.GND
  N1: R1.wiper, Part1.A0
  N2: R1.leg2, C1.+, J2.pin1
  N3: J1.pin1, Part1.5V

notes:
  fingers go here
