# Fritzing sketch simple_resistive_touch_switch (saved by Fritzing 0.9.4)
breadboards: 1

parts:
  Q1 = NPN-Transistor [part_number=2n3904 package="TO92 [THT]"]
  U1 = Arduino Nano (Rev3.0)
  R1 = Resistor [tolerance=±5% resistance=1k package=THT]
  R2 = Resistor [tolerance=±5% resistance=22k package=THT]
  J1 = female pin header, 1 pin [form="♀ (female)"]
  J2 = female pin header, 1 pin [form="♀ (female)"]

nets:
  N1: Q1.E, U1.D2
  N2: Q1.B, R1.Pin_1, R2.Pin_0
  N3: Q1.C, U1.3V3, J2.pin1
  N4: U1.GND, R2.Pin_1
  N5: R1.Pin_0, J1.pin1

notes:
  place fingers here
