# Fritzing sketch touch_switch_darlington_arduino (saved by Fritzing 0.9.4)
breadboards: 1

parts:
  U1 = Arduino Nano (Rev3.0)
  Q1 = NPN-Transistor [part_number=2n3904 package="TO92 [THT]"]
  Q2 = NPN-Transistor [part_number=2n3904 package="TO92 [THT]"]
  R1 = Resistor [tolerance=±5% resistance=100k package=THT]
  R2 = Resistor [tolerance=±5% resistance=220 package=THT]
  LED1 = LED - 5mm [color="Red (633nm)" package="5 mm [THT]"]
  J1 = female pin header, 1 pin [form="♀ (female)"]
  J2 = female pin header, 1 pin [form="♀ (female)"]
  R3 = Resistor [tolerance=±5% resistance=10k package=THT]
  R4 = Resistor [tolerance=±5% resistance=10k package=THT]

nets:
  N1: U1.GND, R1.Pin_0
  N2: U1.D2, Q2.E, R1.Pin_1
  N3: U1.3V3, R2.Pin_1, R4.Pin_1
  N4: Q1.E, Q2.B
  N5: Q1.B, R3.Pin_1
  N6: Q1.C, Q2.C, LED1.cathode
  N7: R2.Pin_0, LED1.anode
  N8: J1.pin1, R3.Pin_0
  N9: J2.pin1, R4.Pin_0

notes:
  place fingers here
