# Fritzing sketch HC-SR04 (saved by Fritzing 0.9.4)
breadboards: 1

parts:
  U1 = Arduino Uno (Rev3)
  HC-SR04_Sensor_1 = HC-SR04 Ultrasonic Distance Sensor

nets:
  N1: U1.D8, HC-SR04_Sensor_1.ECHO
  N2: U1.D9_PWM, HC-SR04_Sensor_1.TRIG
  GND: U1.GND, HC-SR04_Sensor_1.GND
  5V: U1.5V, HC-SR04_Sensor_1.VCC
