# Fritzing sketch HC-SR04_3v3 (saved by Fritzing 0.9.4)
breadboards: 1

parts:
  U1 = Arduino Nano (Rev3.0)
  U2 = Voltage Regulator - 5V [part_number=7805 package="TO220 [THT]"]
  VCC1 = Battery block 9V
  C1 = Electrolytic Capacitor [capacitance=10µF voltage=16V package="100 mil [THT, electrolytic]"]
  C2 = Electrolytic Capacitor [capacitance=1µF voltage=16V package="100 mil [THT, electrolytic]"]
  R1 = Resistor [tolerance=±5% resistance=10k package=THT]
  R2 = Resistor [tolerance=±5% resistance=10k package=THT]
  HC-SR04_Sensor_1 = HC-SR04 Ultrasonic Distance Sensor

nets:
  GND: U1.GND, U2.GND, VCC1.-, C1.-, C2.-, R2.Pin_1, HC-SR04_Sensor_1.GROUND
  N1: U1.D8, R1.Pin_1, R2.Pin_0
  N2: U1.D9, HC-SR04_Sensor_1.TRIG
  N3: U2.input_voltage, VCC1.+, C1.+
  N4: U2.output_voltage, C2.+, HC-SR04_Sensor_1.VCC
  N5: R1.Pin_0, HC-SR04_Sensor_1.ECHO

custom parts:
  HC-SR04 Ultrasonic Distance Sensor: The HC-SR04 is an ultrasonic distance sensor. It is capable of providing measurement for ranges of 2cm to 400cm. The module operates at 5V.
