# Fritzing sketch AnalogSensorsAndVoltageDivider (saved by Fritzing 0.9.4)
breadboards: 1

parts:
  R2 = Photocell (LDR) [package=THT]
  R4 = Resistor [tolerance=±5% resistance=10k package=THT]
  R5 = Resistor [tolerance=±5% resistance=10k package=THT]
  R1 = Rotary Potentiometer (Small) [maximum_resistance=10kΩ package=THT]
  Arduino = Arduino Uno (Rev3)
  R3 = Basic Force Sensing Resistor (FSR) [package=THT]
  part = Basic Force Sensing Resistor (FSR) [package=THT]  # not connected

nets:
  N1: R2.pin_0, R1.leg1, Arduino.5V, R3.pin_0
  N2: R2.pin_1, R4.Pin_1, Arduino.A3
  N3: R4.Pin_0, R5.Pin_0, R1.leg2, Arduino.GND
  N4: R5.Pin_1, Arduino.A0, R3.pin_1
  N5: R1.wiper, Arduino.A5/SCL

notes:
  10k potentiometer
  Photocell or LDR (light-dependant resistor)
  3 examples of voltage dividers
  FSR (force sensitive resistor)
