# Fritzing sketch Analog_sensors_Button (saved by Fritzing 0.9.4)
breadboards: 1

parts:
  U1 = Arduino Uno (Rev3)
  R1 = Resistor [tolerance=±5% resistance=10k package=THT]
  R3 = Resistor [tolerance=±5% resistance=10k package=THT]
  R2 = Resistor [tolerance=±5% resistance=10k package=THT]
  S1 = Pushbutton [package="[THT]"]
  VR1 = Photocell (LDR) [package=THT]
  VR2 = Photocell (LDR) [package=THT]

nets:
  N1: U1.A0, R2.Pin_0, VR1.pin_1
  N2: U1.A1, R3.Pin_0, VR2.pin_1
  N3: U1.GND, R1.Pin_1, R3.Pin_1, R2.Pin_1
  N4: U1.D2, R1.Pin_0, S1.Pin_1, S1.Pin_2
  N5: U1.5V, S1.Pin_3, S1.Pin_4, VR1.pin_0, VR2.pin_0
